// Logisim project problem_1.circ as structural Verilog
module main (
  input  [2:0] in_1,
  output [7:0] out_2
);

  prob3 prob3_1 (.sel(in_1), .display(out_2));
endmodule

// VHDL entity prob1, as the project stores it:
library ieee;
use ieee.std_logic_1164.all;

entity prob1 is
    port(
        a, b, c, d : in std_logic;
        out1, out2 : out std_logic
    );
end entity prob1;

architecture bhv of prob1 is
begin
    out1 <= a and b and c and d;
    out2 <= a or b or c or d;
end architecture bhv;

// VHDL entity prob3, as the project stores it:
library ieee;
use ieee.std_logic_1164.all;

entity prob3 is
    port(
        sel     : in std_logic_vector(2 downto 0);
        display : out std_logic_vector(7 downto 0)
    );
end entity prob3;

architecture bhv of prob3 is
begin
    process(sel)
    begin
        -- 7-segment 순서: a,b,c,d,e,f,g,dp
        case sel is
            when "000" => display <= "11101110"; -- A
            when "001" => display <= "00111110"; -- b
            when "010" => display <= "10011100"; -- C
            when "011" => display <= "01111010"; -- d
            when "100" => display <= "10001110"; -- F
            when "101" => display <= "10111110"; -- g (또는 9)
            when others => display <= "00000000"; -- OFF
        end case;
    end process;
end architecture bhv;
