// Logisim project problem_5.circ as structural Verilog
module project5 (
  input  in_1,
  input  [12:0] in_2,
  output [7:0] out_3
);

  prob5 prob5_1 (.en(in_1), .vt(in_2), .display(out_3));
endmodule

// VHDL entity prob5, as the project stores it:
library ieee;
use ieee.std_logic_1164.all;
use ieee.std_logic_unsigned.all;

entity prob5 is
    port(
        en      : in std_logic;
        vt      : in std_logic_vector(13 downto 1);
        display : out std_logic_vector(7 downto 0)
    );
end entity prob5;

architecture bhv of prob5 is
begin
    process(en, vt)
        variable sum: integer range 0 to 15;
    begin
        if en = '0' then
            display <= "ZZZZZZZZ"; -- High-impedance 상태 (끄기)
        else
            sum := 0;
            for i in 1 to 13 loop
                if (vt(i) = '1') then
                    sum := sum + 1;
                end if;
            end loop;
            
            case sum is
                when 0  => display <= "11111100"; -- 0
                when 1  => display <= "01100000"; -- 1
                when 2  => display <= "11011010"; -- 2
                when 3  => display <= "11110010"; -- 3
                when 4  => display <= "01100110"; -- 4
                when 5  => display <= "10110110"; -- 5
                when 6  => display <= "10111110"; -- 6
                when 7  => display <= "11100000"; -- 7
                when 8  => display <= "11111110"; -- 8
                when 9  => display <= "11110110"; -- 9
                when 10 => display <= "11101110"; -- A
                when 11 => display <= "00111110"; -- b
                when 12 => display <= "10011100"; -- C
                when 13 => display <= "01111010"; -- d
                -- vt가 13비트이므로 14, 15는 도달할 수 없지만 명세(10 to 15) 충족을 위해 포함
                when 14 => display <= "10011110"; -- E
                when 15 => display <= "10001110"; -- F 
                when others => display <= "00000000";
            end case;
        end if;
    end process;
end architecture bhv;
